// Logisim project 11.circ as structural Verilog: 1 circuit, main circuit main
module main (
  input  in_1,
  input  in_2,
  input  in_3,
  input  in_4,
  input  [1:0] in_5,
  output out_6
);

  wire not_1_out;

  not not_1 (not_1_out, in_2);
  Multiplexer #(.select(2)) multiplexer_1 (
    .in0(in_1), .in1(not_1_out), .in2(in_3), .in3(in_4), .out(out_6), .sel(in_5));  // open: en
endmodule
