// Logisim project 4.circ as structural Verilog: 1 circuit, main circuit main
module main (
  input  A,
  input  A_2,
  input  B,
  input  B_2,
  input  A_3,
  input  A_4,
  input  B_3,
  input  B_4,
  output out_9,
  output out_10,
  output out_11,
  output out_12
);

  wire and_1_out, not_3_out, not_4_out, not_5_out, not_6_out, or_1_out;

  or or_1 (or_1_out, A, B);
  and and_1 (and_1_out, A_3, B_3);
  not not_1 (out_9, or_1_out);
  not not_2 (out_11, and_1_out);
  not not_3 (not_3_out, A_2);
  not not_4 (not_4_out, B_2);
  not not_5 (not_5_out, A_4);
  not not_6 (not_6_out, B_4);
  buf and_2 (out_10, not_4_out);  // AND_Gate
  or or_2 (out_12, not_5_out, not_6_out);
endmodule
